# Fritzing sketch home_food_v2 (saved by Fritzing 0.9.3b)
circuit board: 8.46667cm x 5.64444cm

parts:
  12V_power_source = Power plug
  DHT11 = DHT11 Humitidy and Temperature Sensor
  DS1307_AT24C32 = Adafruit DS1307 RTC Breakout [part_number="with EEPROM 32k"]
  WeMos_D1_Mini1 = WeMos D1 Mini
  M2 = Stepper Motor - Bipolar
  DRV_1 = DRV 8825 Stepper Motor Carrier, High Current [part_number="DRV 8825"]
  M3 = RioRand LM2596

nets:
  N1: 12V_power_source.GND, DRV_1.GROUND_ST/_MT, M3.Pin_2
  N2: 12V_power_source.VCC, DRV_1.VOLTAGE_ST/_MT, M3.Pin_1
  VDD: DHT11.VDD, DS1307_AT24C32.VCC, WeMos_D1_Mini1.5V, M3.Pin_3
  N3: DHT11.DATA, WeMos_D1_Mini1.D5
  GND: DHT11.GND, DS1307_AT24C32.GND
  N4: DS1307_AT24C32.SCL, WeMos_D1_Mini1.D1
  N5: DS1307_AT24C32.SDA, WeMos_D1_Mini1.D2
  N6: WeMos_D1_Mini1.D0, WeMos_D1_Mini1.RST
  N7: WeMos_D1_Mini1.D6, DRV_1.DIRECTION
  N8: WeMos_D1_Mini1.D7, DRV_1.STEP
  N9: WeMos_D1_Mini1.D8, DRV_1.SLEEP
  N10: WeMos_D1_Mini1.G, DRV_1.ENABLE, M3.Pin_4
  N11: M2.A, DRV_1.OUT_2B
  N12: M2.C, DRV_1.OUT_2A
  N13: M2.B, DRV_1.OUT_1A
  N14: M2.D, DRV_1.OUT_1B

custom parts:
  DHT11 Humitidy and Temperature Sensor: DHT11 Humidity and Temperature Sensor
  Adafruit DS1307 RTC Breakout: This is a great battery-backed real time clock (RTC) that allows your microcontroller project to keep track of time even if it is reprogrammed, or if the power is lost. Perfect for datalogging, clock-building, time stamping, timers and alarms, etc. The DS1307 is the most popular RTC - but it requires 5V power to work (although we've used it with 5V power and 3.3V logic successfully) PCB &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
